# Fritzing sketch P2 (saved by Fritzing 0.9.10b)
breadboards: 1

parts:
  Mod1 = Raspberry Pi Pico W
  LED1 = LED - 3mm [color="Red (633nm)" current=0.030 package="3 mm [THT]"]
  R1 = Resistor [tolerance=±5% resistance=10k package="0805 [SMD]"]
  R2 = PHOTOCELL [package=photocell]
  R3 = Resistor [tolerance=±5% resistance=10k package="0805 [SMD]"]
  DS1 = DS18B20 1-Wire Temperature Sensor [part_number=DS18B20]
  M1 = Dagu DGServo 9g (Pan and tilt) [part_number=RS001B]
  HC-SR04_Sensor_1 = HC-SR04 Ultrasonic Distance Sensor
  R4 = Resistor [tolerance=±5% resistance=10k package="0805 [SMD]"]
  R5 = Resistor [tolerance=±5% resistance=10k package="0805 [SMD]"]

nets:
  GND: Mod1.pin_3, Mod1.pin_8, Mod1.pin_13, Mod1.pin_18, Mod1.pin_23, Mod1.pin_28, Mod1.pin_33, Mod1.pin_38, Mod1.pin_42, R1.Pin_1, R3.Pin_1, DS1.GND, M1.gnd, HC-SR04_Sensor_1.GND
  N1: Mod1.pin_6, DS1.DQ
  N2: Mod1.pin_19, HC-SR04_Sensor_1.TRIG
  N3: Mod1.pin_20, R4.Pin_1, R5.Pin_0
  N4: Mod1.pin_21, M1.pulse
  N5: Mod1.pin_22, LED1.cathode
  N6: Mod1.pin_34, R2.P$2, R3.Pin_0
  N7: Mod1.pin_36, R2.P$1, DS1.VDD
  VCC: Mod1.pin_39, M1.vcc, HC-SR04_Sensor_1.VCC
  N8: LED1.anode, R1.Pin_0
  N9: HC-SR04_Sensor_1.ECHO, R4.Pin_0

custom parts:
  Raspberry Pi Pico W: Raspberry Pi Pico W. Based around the RP2040 microcontroller the Pico W is a low cost microcontroller device bringing Raspberry Pi quality, cost, and easy of use to the microcontroller space. The areas marked KEEPOUT in pcb silkscreen should not have traces running through them to avoid shorts on a soldered in module!
